# Fritzing sketch connections scheme - v1 (saved by Fritzing 0.9.3b)

parts:
  S1 = H-Bridge with L298N
  Componente3 = Adafruit Ultimate GPS Logger Shield [part_number="Adafruit #1272"]
  Componente4 = Arduino Uno (Rev3) - ICSP
  hc-sr1 = hc-sr04
  M1 = DC Motor
  M2 = DC Motor
  Componente5 = NRF24L01
  VCC2 = 4 x AAA Battery Mount
  VCC1 = 4 x AAA Battery Mount
  GY-1 = GY-271 [part_number=GY-271]

nets:
  N1: S1.12V, VCC1.+
  GND: S1.GND, Componente3.GND, Componente3.N$17, Componente3.N$18, Componente3.N$19, Componente3.N$20, Componente3.N$23, Componente3.N$51, Componente3.N$63, Componente3.N$72, Componente3.N$74, Componente3.N$173, Componente3.N$185, Componente3.N$186, Componente4.GND, hc-sr1.GND, Componente5.GND, VCC2.-, VCC1.-, GY-1.GND
  N2: S1.ENA, Componente3.D6, Componente4.D6_PWM
  N3: S1.IN1, Componente3.A0, Componente4.A0
  N4: S1.IN2, Componente3.A1, Componente4.A1
  N5: S1.IN3, Componente3.A2, Componente4.A2
  N6: S1.IN4, Componente3.A3, Componente4.A3
  N7: S1.ENB, Componente3.D5, Componente4.D5_PWM
  N8: S1.M1-01, M1.pin_2
  N9: S1.M1-02, M1.pin_1
  N10: S1.M2-01, M2.pin_2
  N11: S1.M2-02, M2.pin_1
  N12: Componente3.RESET, Componente4.RESET
  VCC: Componente3.+5V, Componente3.N$79, Componente3.N$80, Componente3.N$81, Componente3.N$82, Componente3.N$83, Componente4.5V, hc-sr1.VCC, GY-1.VCC
  VIN: Componente3.VIN, Componente4.VIN, VCC2.+
  N13: Componente3.D3, Componente4.D3_PWM, hc-sr1.Echo
  N14: Componente3.D4, Componente4.D4, hc-sr1.Trig
  N15: Componente3.A4, Componente3.SDA, Componente4.A4/SDA, GY-1.SDA
  N16: Componente3.A5, Componente3.SCL, Componente4.A5/SCL, GY-1.SCL
  N17: Componente3.SCK, Componente4.D13/SCK, Componente5.SCK
  N18: Componente3.MISO, Componente4.ICSP_MISO, Componente4.D12/MISO, Componente5.MISO
  N19: Componente3.MOSI, Componente4.D11_PWM/MOSI, Componente5.MOSI
  N20: Componente3.SD_CS, Componente4.D10_PWM/SS, Componente5.CSN
  N21: Componente3.D9, Componente4.D9_PWM, Componente5.CE
  3V3: Componente3.3V, Componente4.3V3, Componente5.VCC
  N22: Componente3.AREF, Componente4.AREF
  N23: Componente3.D0, Componente4.D0/RX
  N24: Componente3.D1, Componente4.D1/TX
  N25: Componente3.D2, Componente4.D2
  N26: Componente3.D7, Componente4.D7
  N27: Componente3.D8, Componente4.D8
  N28: Componente3.IOREF, Componente4.IOREF
  N29: Componente3.NC, Componente4.N/C

custom parts:
  H-Bridge with L298N: h-bridge
  Adafruit Ultimate GPS Logger Shield: Brand new and better than ever, we've replaced our Adafruit GPS shield kit with this assembled shield that comes with an Ultimate GPS module. This GPS shield works great with either UNO or Leonardo Arduinos and is designed to log data to an SD card. Or you can leave the SD card out and use the GPS for a geocaching project, or maybe a music player that changes tunes depending on where you are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
  GY-271: GY-271 - Electronic compass module - 3 Axis Magnetic Field Sensor HMC5883L
